// Logisim project project4.circ as structural Verilog: 7 circuits, main circuit MAIN
module _1b_ALU (
  input  A_invert,
  input  B_invert,
  input  C_in,
  input  [1:0] OP2,
  input  A,
  input  B,
  input  Less,
  output RESULT,
  output Set__MSB_only,
  output Overflow__MSB_only,
  output C_out
);

  wire adder_1_out, and_1_out, or_1_out, xor_1_out, xor_2_out;

  xor xor_1 (xor_1_out, A_invert, A);
  xor xor_2 (xor_2_out, B_invert, B);
  and and_1 (and_1_out, xor_1_out, xor_2_out);
  or or_1 (or_1_out, xor_1_out, xor_2_out);
  Adder #(.width(1)) adder_1 (.a(xor_1_out), .b(xor_2_out), .out(adder_1_out), .cin(C_in), .cout(C_out));
  Multiplexer #(.select(2), .enable("false")) multiplexer_1 (
    .in0(and_1_out), .in1(or_1_out), .in2(adder_1_out), .in3(Less), .out(RESULT), .sel(OP2));
  xor xor_3 (Overflow__MSB_only, C_in, C_out);
  xor xor_4 (Set__MSB_only, adder_1_out, Overflow__MSB_only);

  // Notes on the sheet:
  //   1 Bit ALU
endmodule

// ALU
module _8_bit_ALU (
  input  [3:0] _4_bit_ALU_control,
  input  [7:0] A,
  input  [7:0] B,
  output [7:0] Result,
  output Zero,
  output Overflow,
  output Cout
);

  wire n1b_alu_1_c_out, n1b_alu_2_c_out, n1b_alu_3_c_out, n1b_alu_4_c_out, n1b_alu_5_c_out, n1b_alu_6_c_out,
       n1b_alu_7_c_out, Set;

  Hex_Digit_Display hex_digit_display_1 (.value(A[7:4]));  // open: dp
  Hex_Digit_Display hex_digit_display_2 (.value(A[3:0]));  // open: dp
  Hex_Digit_Display hex_digit_display_3 (.value(B[3:0]));  // open: dp
  Hex_Digit_Display hex_digit_display_4 (.value(B[7:4]));  // open: dp
  Hex_Digit_Display hex_digit_display_5 (.value(_4_bit_ALU_control));  // open: dp
  _1b_ALU u_1b_alu_1 (
    .A(A[0]), .B(B[0]), .Less(Set), .RESULT(Result[0]), .A_invert(_4_bit_ALU_control[3]),
    .B_invert(_4_bit_ALU_control[2]), .C_in(_4_bit_ALU_control[2]), .OP2(_4_bit_ALU_control[1:0]),
    .C_out(n1b_alu_1_c_out));  // open: Set__MSB_only, Overflow__MSB_only
  _1b_ALU u_1b_alu_2 (
    .A(A[1]), .B(B[1]), .Less(1'b0), .RESULT(Result[1]), .A_invert(_4_bit_ALU_control[3]),
    .B_invert(_4_bit_ALU_control[2]), .C_in(n1b_alu_1_c_out), .OP2(_4_bit_ALU_control[1:0]),
    .C_out(n1b_alu_2_c_out));  // open: Set__MSB_only, Overflow__MSB_only
  _1b_ALU u_1b_alu_3 (
    .A(A[2]), .B(B[2]), .Less(1'b0), .RESULT(Result[2]), .A_invert(_4_bit_ALU_control[3]),
    .B_invert(_4_bit_ALU_control[2]), .C_in(n1b_alu_2_c_out), .OP2(_4_bit_ALU_control[1:0]),
    .C_out(n1b_alu_3_c_out));  // open: Set__MSB_only, Overflow__MSB_only
  _1b_ALU u_1b_alu_4 (
    .A(A[3]), .B(B[3]), .Less(1'b0), .RESULT(Result[3]), .A_invert(_4_bit_ALU_control[3]),
    .B_invert(_4_bit_ALU_control[2]), .C_in(n1b_alu_3_c_out), .OP2(_4_bit_ALU_control[1:0]),
    .C_out(n1b_alu_4_c_out));  // open: Set__MSB_only, Overflow__MSB_only
  _1b_ALU u_1b_alu_5 (
    .A(A[4]), .B(B[4]), .Less(1'b0), .RESULT(Result[4]), .A_invert(_4_bit_ALU_control[3]),
    .B_invert(_4_bit_ALU_control[2]), .C_in(n1b_alu_4_c_out), .OP2(_4_bit_ALU_control[1:0]),
    .C_out(n1b_alu_5_c_out));  // open: Set__MSB_only, Overflow__MSB_only
  _1b_ALU u_1b_alu_6 (
    .A(A[5]), .B(B[5]), .Less(1'b0), .RESULT(Result[5]), .A_invert(_4_bit_ALU_control[3]),
    .B_invert(_4_bit_ALU_control[2]), .C_in(n1b_alu_5_c_out), .OP2(_4_bit_ALU_control[1:0]),
    .C_out(n1b_alu_6_c_out));  // open: Set__MSB_only, Overflow__MSB_only
  _1b_ALU u_1b_alu_7 (
    .A(A[6]), .B(B[6]), .Less(1'b0), .RESULT(Result[6]), .A_invert(_4_bit_ALU_control[3]),
    .B_invert(_4_bit_ALU_control[2]), .C_in(n1b_alu_6_c_out), .OP2(_4_bit_ALU_control[1:0]),
    .C_out(n1b_alu_7_c_out));  // open: Set__MSB_only, Overflow__MSB_only
  _1b_ALU u_1b_alu_8 (
    .A(A[7]), .B(B[7]), .Less(1'b0), .RESULT(Result[7]), .A_invert(_4_bit_ALU_control[3]),
    .B_invert(_4_bit_ALU_control[2]), .C_in(n1b_alu_7_c_out), .OP2(_4_bit_ALU_control[1:0]), .C_out(Cout),
    .Set__MSB_only(Set), .Overflow__MSB_only(Overflow));
  Hex_Digit_Display hex_digit_display_6 (.value(Result[7:4]));  // open: dp
  Hex_Digit_Display hex_digit_display_7 (.value(Result[3:0]));  // open: dp
  nor nor_1 (Zero, Result[0], Result[1], Result[2], Result[3], Result[4], Result[5], Result[6], Result[7]);

  // Other names for the same wires on the sheet: ALU_ctrl[3:0] = _4_bit_ALU_control;
  //   OP[1:0] = _4_bit_ALU_control[1:0]; Binv = _4_bit_ALU_control[2]; Ainv = _4_bit_ALU_control[3];
  //   Operand_A[7:0] = A; Operand_B[7:0] = B; OV = Overflow

  // Notes on the sheet:
  //   Input A
  //   Input B
  //   Result
endmodule

// CLR
module MAIN (
  output [15:0] Instruction
);

  wire AeqB, ALUSrc, BEQ, BNE, clk, CLR, CLR_out, comparator_1_lt, comparator_2_eq, comparator_3_eq,
       comparator_4_eq, comparator_5_eq, comparator_6_eq, comparator_7_eq, comparator_8_eq, comparator_9_eq,
       counter_1_q, Cout, instruction_decoder_1_alusrc, instruction_decoder_1_memread,
       instruction_decoder_1_memwrite, instruction_decoder_1_regwrite, J, MemRead, MemtoReg, MemWrite,
       NEXT_TEST_CASE_out, Overflow, RegDst, RegDst1, register_5_q, register_6_q, register_8_q,
       register_25_q, RegWrite, Reset_Testcase_out, ZERO;
  wire [2:0] multiplexer_2_out, Rd, Rd1, register_26_q, Rs, Rs1, Rt, Rt1, WriteRegister;
  wire [3:0] ALUcontrol, instruction_decoder_1_alucontrol, Test_Case_Number;
  wire [5:0] immd, immd1;
  wire [7:0] ALUResult, ALUResult_ADDRESS, bit_extender_1_out, DataToMem, ExpectedR1, ExpectedR2, ExpectedR3,
       ExpectedR4, ExpectedR5, ExpectedR6, ExpectedR7, JumpAddress, MaxPC, MemReadData, multiplexer_1_out,
       NextPC, PC, PC1, r0, r0_prime, r1, r1_prime, r2, r2_prime, r3, r3_prime, r4, r4_prime, r5, r5_prime,
       r6, r6_prime, r7, r7_prime, ram_1_data, ReadData1, ReadData2, register_28_q, WriteData;
  wire [15:0] test_cases_xxx_fill_in_1_instr;

  Button NEXT_TEST_CASE (.out(NEXT_TEST_CASE_out));
  Button Reset_Testcase (.out(Reset_Testcase_out));
  Clock CLOCK (.out(clk));
  Button u_CLR (.out(CLR_out));
  or or_1 (CLR, NEXT_TEST_CASE_out, Reset_Testcase_out, CLR_out);
  Counter #(.width(4), .max('h9)) u_Test_Case_Number (
    .Q(Test_Case_Number), .clk(NEXT_TEST_CASE_out), .clr(Reset_Testcase_out));  // open: load, D, count, carry
  Hex_Digit_Display hex_digit_display_1 (.value(Test_Case_Number));  // open: dp
  LED checkMaxPC (.in(comparator_1_lt));
  Comparator comparator_1 (.a(PC1), .b(MaxPC), .lt(comparator_1_lt));  // open: gt, eq
  Hex_Digit_Display hex_digit_display_2 (.value(PC1[7:4]));  // open: dp
  Hex_Digit_Display hex_digit_display_3 (.value(PC1[3:0]));  // open: dp
  Register u_PC (.D(NextPC), .Q(PC), .clk(clk), .clr(CLR));  // open: en
  Hex_Digit_Display hex_digit_display_4 (.value(Instruction[15:12]));  // open: dp
  Hex_Digit_Display hex_digit_display_5 (.value(Instruction[11:8]));  // open: dp
  LED checkR1 (.in(comparator_2_eq));
  Comparator comparator_2 (.a(r1), .b(ExpectedR1), .eq(comparator_2_eq));  // open: gt, lt
  Hex_Digit_Display hex_digit_display_6 (.value(r1[3:0]));  // open: dp
  Hex_Digit_Display hex_digit_display_7 (.value(r1[7:4]));  // open: dp
  Hex_Digit_Display hex_digit_display_8 (.value(Instruction[7:4]));  // open: dp
  Hex_Digit_Display hex_digit_display_9 (.value(r2[7:4]));  // open: dp
  Hex_Digit_Display hex_digit_display_10 (.value(Instruction[3:0]));  // open: dp
  Hex_Digit_Display hex_digit_display_11 (.value(r2[3:0]));  // open: dp
  Comparator #(.width(16)) comparator_3 (.a(16'hefff), .b(Instruction), .eq(comparator_3_eq));  // open: gt, lt
  LED checkR2 (.in(comparator_4_eq));
  Comparator comparator_4 (.a(r2), .b(ExpectedR2), .eq(comparator_4_eq));  // open: gt, lt
  Hex_Digit_Display hex_digit_display_12 (.value(r3[7:4]));  // open: dp
  Test_Cases__XXX_FILL_IN test_cases_xxx_fill_in_1 (
    .PC(PC), .testCase(Test_Case_Number), .ExpectedR1(ExpectedR1), .ExpectedR2(ExpectedR2),
    .ExpectedR3(ExpectedR3), .ExpectedR4(ExpectedR4), .ExpectedR5(ExpectedR5), .ExpectedR6(ExpectedR6),
    .ExpectedR7(ExpectedR7), .instr(test_cases_xxx_fill_in_1_instr), .MaxPC(MaxPC));
  LED FINISHED (.in(counter_1_q));
  Counter #(.width(1), .max('h1), .ongoal("stay"), .trigger("falling")) counter_1 (
    .Q(counter_1_q), .clk(comparator_3_eq), .clr(CLR));  // open: load, D, count, carry
  Comparator comparator_5 (.a(r3), .b(ExpectedR3), .eq(comparator_5_eq));  // open: gt, lt
  Hex_Digit_Display hex_digit_display_13 (.value(r3[3:0]));  // open: dp
  LED checkR3 (.in(comparator_5_eq));
  Hex_Digit_Display hex_digit_display_14 (.value(r4[7:4]));  // open: dp
  Hex_Digit_Display hex_digit_display_15 (.value(r4[3:0]));  // open: dp
  LED checkR4 (.in(comparator_6_eq));
  Comparator comparator_6 (.a(r4), .b(ExpectedR4), .eq(comparator_6_eq));  // open: gt, lt
  Register #(.width(16)) register_1 (
    .D(test_cases_xxx_fill_in_1_instr), .Q(Instruction), .clk(clk), .clr(CLR));  // open: en
  Register register_2 (.D(PC), .Q(PC1), .clk(clk), .clr(CLR));  // open: en
  Hex_Digit_Display hex_digit_display_16 (.value(r5[3:0]));  // open: dp
  Hex_Digit_Display hex_digit_display_17 (.value(r5[7:4]));  // open: dp
  LED checkR5 (.in(comparator_7_eq));
  Comparator comparator_7 (.a(r5), .b(ExpectedR5), .eq(comparator_7_eq));  // open: gt, lt
  Hex_Digit_Display hex_digit_display_18 (.value(r6[7:4]));  // open: dp
  Instruction_Decoder instruction_decoder_1 (
    .Rs(Rs), .Rt(Rt), .Rd(Rd), .instr(Instruction), .immediate(immd), .ALUSrc(instruction_decoder_1_alusrc),
    .RegDst(RegDst), .MemWrite(instruction_decoder_1_memwrite),
    .ALUcontrol(instruction_decoder_1_alucontrol), .RegWrite(instruction_decoder_1_regwrite),
    .MemRead(instruction_decoder_1_memread), .BEQ(BEQ), .BNE(BNE), .J(J), .iumpAddress(JumpAddress));  // open: MemtoReg
  Comparator comparator_8 (.a(r6), .b(ExpectedR6), .eq(comparator_8_eq));  // open: gt, lt
  Hex_Digit_Display hex_digit_display_19 (.value(r6[3:0]));  // open: dp
  registerFile__XXX_FILL_IN registerfile_xxx_fill_in_1 (
    .r0(r0_prime), .r1(r1_prime), .r2(r2_prime), .r3(r3_prime), .r4(r4_prime), .r5(r5_prime), .r6(r6_prime),
    .r7(r7_prime), .Rs(Rs), .Rt(Rt), .WriteData(WriteData), .WriteRegister(WriteRegister),
    .RegWrite(RegWrite), .Clk(clk), .CLR(CLR), .AeqB(AeqB));
  LED checkR6 (.in(comparator_8_eq));
  NextPC__XXX_FILL_IN nextpc_xxx_fill_in_1 (
    .jumpAddress(JumpAddress), .PC_prime(PC1), .AeqB(AeqB), .BEQ(BEQ), .BNE(BNE), .J(J), .immd(immd),
    .PC(PC), .NextPC(NextPC));
  Hex_Digit_Display hex_digit_display_20 (.value(r7[7:4]));  // open: dp
  Hex_Digit_Display hex_digit_display_21 (.value(r7[3:0]));  // open: dp
  LED checkR7 (.in(comparator_9_eq));
  Comparator comparator_9 (.a(r7), .b(ExpectedR7), .eq(comparator_9_eq));  // open: gt, lt
  Register #(.width(6)) register_3 (.D(immd), .Q(immd1), .clk(clk), .clr(CLR));  // open: en
  Register #(.width(1)) register_4 (.D(instruction_decoder_1_alusrc), .Q(ALUSrc), .clk(clk), .clr(CLR));  // open: en
  Register #(.width(1)) register_5 (
    .D(instruction_decoder_1_memwrite), .Q(register_5_q), .clk(clk), .clr(CLR));  // open: en
  Register #(.width(1)) register_6 (
    .D(instruction_decoder_1_memread), .Q(register_6_q), .clk(clk), .clr(CLR));  // open: en
  Register #(.width(4)) register_7 (
    .D(instruction_decoder_1_alucontrol), .Q(ALUcontrol), .clk(clk), .clr(CLR));  // open: en
  Register #(.width(1)) register_8 (
    .D(instruction_decoder_1_regwrite), .Q(register_8_q), .clk(clk), .clr(CLR));  // open: en
  Register #(.width(1)) register_9 (.D(RegDst), .Q(RegDst1), .clk(clk), .clr(CLR));  // open: en
  Register #(.width(3)) register_10 (.D(Rs), .Q(Rs1), .clk(clk), .clr(CLR));  // open: en
  Register #(.width(3)) register_11 (.D(Rt), .Q(Rt1), .clk(clk), .clr(CLR));  // open: en
  Register #(.width(3)) register_12 (.D(Rd), .Q(Rd1), .clk(clk), .clr(CLR));  // open: en
  Register register_13 (.D(r0_prime), .Q(r0), .clk(clk), .clr(CLR));  // open: en
  Register register_14 (.D(r1_prime), .Q(r1), .clk(clk), .clr(CLR));  // open: en
  Register register_15 (.D(r2_prime), .Q(r2), .clk(clk), .clr(CLR));  // open: en
  Register register_16 (.D(r3_prime), .Q(r3), .clk(clk), .clr(CLR));  // open: en
  Register register_17 (.D(r4_prime), .Q(r4), .clk(clk), .clr(CLR));  // open: en
  Register register_18 (.D(r5_prime), .Q(r5), .clk(clk), .clr(CLR));  // open: en
  Register register_19 (.D(r6_prime), .Q(r6), .clk(clk), .clr(CLR));  // open: en
  Register register_20 (.D(r7_prime), .Q(r7), .clk(clk), .clr(CLR));  // open: en
  assign bit_extender_1_out = {{2{immd1[5]}}, immd1};  // Bit_Extender bit_extender_1
  Multiplexer #(.width(8), .enable("false")) multiplexer_1 (
    .in0(ReadData2), .in1(bit_extender_1_out), .out(multiplexer_1_out), .sel(ALUSrc));
  Multiplexer #(.width(3), .enable("false")) multiplexer_2 (
    .in0(Rt1), .in1(Rd1), .out(multiplexer_2_out), .sel(RegDst1));
  Multiplexer #(.select(3), .width(8), .enable("false")) multiplexer_3 (
    .in0(r0), .in1(r1), .in2(r2), .in3(r3), .in4(r4), .in5(r5), .in6(r6), .in7(r7), .out(ReadData1), .sel(Rs1));
  Multiplexer #(.select(3), .width(8), .enable("false")) multiplexer_4 (
    .in0(r0), .in1(r1), .in2(r2), .in3(r3), .in4(r4), .in5(r5), .in6(r6), .in7(r7), .out(ReadData2), .sel(Rt1));
  _8_bit_ALU u_8_bit_alu_1 (
    ._4_bit_ALU_control(ALUcontrol), .A(ReadData1), .Result(ALUResult), .Zero(ZERO), .B(multiplexer_1_out),
    .Overflow(Overflow), .Cout(Cout));
  Register register_21 (.D(ReadData2), .Q(DataToMem), .clk(clk), .clr(CLR));  // open: en
  Register register_22 (.D(ALUResult), .Q(ALUResult_ADDRESS), .clk(clk), .clr(CLR));  // open: en
  Register #(.width(1)) register_23 (.D(register_5_q), .Q(MemWrite), .clk(clk), .clr(CLR));  // open: en
  Register #(.width(1)) register_24 (.D(register_6_q), .Q(MemRead), .clk(clk), .clr(CLR));  // open: en
  Register #(.width(1)) register_25 (.D(register_8_q), .Q(register_25_q), .clk(clk), .clr(CLR));  // open: en
  Register #(.width(3)) register_26 (.D(multiplexer_2_out), .Q(register_26_q), .clk(clk), .clr(CLR));  // open: en
  RAM #(.bus("separate")) ram_1 (
    .addr(ALUResult_ADDRESS), .din(DataToMem), .data(ram_1_data), .str(MemWrite), .sel(1'b1), .clk(clk),
    .ld(MemRead), .clr(CLR));
  Register register_27 (.D(ram_1_data), .Q(MemReadData), .clk(clk), .clr(CLR));  // open: en
  Register register_28 (.D(ALUResult_ADDRESS), .Q(register_28_q), .clk(clk), .clr(CLR));  // open: en
  Register #(.width(1)) register_29 (.D(MemRead), .Q(MemtoReg), .clk(clk), .clr(CLR));  // open: en
  Register #(.width(1)) register_30 (.D(register_25_q), .Q(RegWrite), .clk(clk), .clr(CLR));  // open: en
  Register #(.width(3)) register_31 (.D(register_26_q), .Q(WriteRegister), .clk(clk), .clr(CLR));  // open: en
  Multiplexer #(.width(8), .enable("false")) multiplexer_5 (
    .in0(register_28_q), .in1(MemReadData), .out(WriteData), .sel(MemtoReg));

  // Notes on the sheet:
  //   (XXX FILL IN)	
  //   (XXX FILL IN)	
  //   Submission by Lwin Moe, Linh Pham, and Rongjie Mai
  //   (XXX FILL IN)	
  //   (XXX FILL IN)	
  //   (XXX FILL IN)	
  //   (XXX FILL IN)	
  //   (XXX FILL IN)	
  //   (XXX FILL IN)	
  //   (XXX FILL IN)	
  //   (XXX FILL IN)	
  //   (XXX FILL IN)	
  //   (XXX FILL IN)	
  //   (XXX FILL IN)	
  //   (XXX FILL IN)	
  //   (XXX FILL IN)	
  //   (XXX FILL IN)	
  //   (XXX FILL IN)	
  //   (XXX FILL IN)	
  //   (XXX FILL IN)	
  //   (XXX FILL IN)	
  //   (XXX FILL IN)
  //   (XXX FILL IN)
  //   (XXX FILL IN)
  //   (XXX FILL IN)
  //   (XXX FILL IN)
  //   (XXX FILL IN)
  //   Data Memory
  //   (XXX FILL IN)
  //   (XXX FILL IN)
  //   (XXX FILL IN)
  //   (XXX FILL IN)
  //   (XXX FILL IN)
endmodule

module NextPC__XXX_FILL_IN (
  input  [7:0] jumpAddress,
  input  [7:0] PC,
  input  [5:0] immd,
  input  [7:0] PC_prime,
  input  AeqB,
  input  BEQ,
  input  BNE,
  input  J,
  output [7:0] NextPC
);

  wire and_1_out, and_2_out, not_1_out, or_1_out;
  wire [7:0] adder_1_out, adder_2_out, adder_3_out, bit_extender_1_out, multiplexer_1_out;

  assign bit_extender_1_out = {{2{immd[5]}}, immd};  // Bit_Extender bit_extender_1
  Adder adder_1 (.a(8'h1), .b(PC_prime), .out(adder_1_out));  // open: cin, cout
  Adder adder_2 (.a(PC), .b(8'h1), .out(adder_2_out));  // open: cin, cout
  Adder adder_3 (.a(bit_extender_1_out), .b(adder_1_out), .out(adder_3_out));  // open: cin, cout
  and and_1 (and_1_out, AeqB, BEQ);
  not not_1 (not_1_out, AeqB);
  and and_2 (and_2_out, not_1_out, BNE);
  or or_1 (or_1_out, and_1_out, and_2_out);
  Multiplexer #(.width(8), .enable("false")) multiplexer_1 (
    .in0(adder_2_out), .in1(adder_3_out), .out(multiplexer_1_out), .sel(or_1_out));
  Multiplexer #(.width(8), .enable("false")) multiplexer_2 (
    .in0(multiplexer_1_out), .in1(jumpAddress), .out(NextPC), .sel(J));

  // Notes on the sheet:
  //   (used to compute PC+1)
  //   (used to compute  the branch target address)
  //   Submission by Lwin Moe, Linh Pham, and Rongjie Mai
endmodule

module registerFile__XXX_FILL_IN (
  input  [2:0] Rs,
  input  [2:0] Rt,
  input  [7:0] WriteData,
  input  [2:0] WriteRegister,
  input  RegWrite,
  input  Clk,
  input  CLR,
  output [7:0] r0,
  output [7:0] r1,
  output [7:0] r2,
  output [7:0] r3,
  output [7:0] r4,
  output [7:0] r5,
  output [7:0] r6,
  output [7:0] r7,
  output AeqB
);

  wire and_1_out, and_2_out, and_3_out, and_4_out, and_5_out, and_6_out, and_7_out, en1, en2, en3, en4, en5,
       en6, en7;
  wire [7:0] multiplexer_1_out, multiplexer_2_out;

  Demultiplexer #(.select(3), .enable("false")) demultiplexer_1 (
    .out1(en1), .out2(en2), .out3(en3), .out4(en4), .out5(en5), .out6(en6), .out7(en7), .in(RegWrite),
    .sel(WriteRegister));  // open: out0
  and and_1 (and_1_out, RegWrite, en1);
  and and_2 (and_2_out, RegWrite, en2);
  and and_3 (and_3_out, RegWrite, en3);
  and and_4 (and_4_out, RegWrite, en4);
  and and_5 (and_5_out, RegWrite, en5);
  and and_6 (and_6_out, RegWrite, en6);
  and and_7 (and_7_out, RegWrite, en7);
  Register #(.trigger("falling")) register_1 (.D(WriteData), .en(and_1_out), .Q(r1), .clk(Clk), .clr(CLR));
  Register #(.trigger("falling")) register_2 (.D(WriteData), .en(and_2_out), .Q(r2), .clk(Clk), .clr(CLR));
  Register #(.trigger("falling")) register_3 (.D(WriteData), .en(and_3_out), .Q(r3), .clk(Clk), .clr(CLR));
  Register #(.trigger("falling")) register_4 (.D(WriteData), .en(and_4_out), .Q(r4), .clk(Clk), .clr(CLR));
  Register #(.trigger("falling")) register_5 (.D(WriteData), .en(and_5_out), .Q(r5), .clk(Clk), .clr(CLR));
  Register #(.trigger("falling")) register_6 (.D(WriteData), .en(and_6_out), .Q(r6), .clk(Clk), .clr(CLR));
  Register #(.trigger("falling")) register_7 (.D(WriteData), .en(and_7_out), .Q(r7), .clk(Clk), .clr(CLR));
  Multiplexer #(.select(3), .width(8), .enable("false")) multiplexer_1 (
    .in0({8{1'b0}}), .in1(r1), .in2(r2), .in3(r3), .in4(r4), .in5(r5), .in6(r6), .in7(r7),
    .out(multiplexer_1_out), .sel(Rs));
  Multiplexer #(.select(3), .width(8), .enable("false")) multiplexer_2 (
    .in0({8{1'b0}}), .in1(r1), .in2(r2), .in3(r3), .in4(r4), .in5(r5), .in6(r6), .in7(r7),
    .out(multiplexer_2_out), .sel(Rt));
  Comparator comparator_1 (.a(multiplexer_1_out), .b(multiplexer_2_out), .eq(AeqB));  // open: gt, lt

  assign r0 = {8{1'b0}};

  // Other names for the same wires on the sheet: RegW = RegWrite

  // Notes on the sheet:
  //   ALUSrc=A'BC'+B'CD				
  //   Submission by Lwin Moe, Linh Pham, and Rongjie Mai
  //   Regsiters should be falling edge triggered
  //   (Registers can be written in the first half cycle)
  //   (and then be read in  in the second half cycle)
endmodule

module Instruction_Decoder (
  input  [15:0] instr,
  output [2:0] Rs,
  output [2:0] Rt,
  output [2:0] Rd,
  output [5:0] immediate,
  output [7:0] iumpAddress,
  output BEQ,
  output BNE,
  output ALUSrc,
  output RegDst,
  output J,
  output MemWrite,
  output MemRead,
  output MemtoReg,
  output [3:0] ALUcontrol,
  output RegWrite
);

  wire A_prime_BC_prime_out, AB_prime_D_out, ADD, ADDI, AND, and_1_out, and_2_out, and_3_out, and_4_out,
       and_5_out, and_6_out, and_7_out, and_8_out, and_9_out, and_10_out, and_11_out, and_12_out, and_13_out,
       and_15_out, and_16_out, and_17_out, B_prime_CD_out, SLT, SUB;

  and and_1 (and_1_out, instr[14], instr[13]);
  and and_2 (and_2_out, instr[14], instr[12]);
  and and_3 (and_3_out, instr[15], ~instr[14], ~instr[12]);  // AND_Gate
  and and_4 (and_4_out, instr[15], instr[14]);
  and and_5 (and_5_out, ~instr[15], instr[14]);  // AND_Gate
  and and_6 (and_6_out, ~instr[15], ~instr[14], ~instr[13], instr[12]);  // AND_Gate
  and and_7 (and_7_out, instr[14], instr[13], instr[12]);
  and and_8 (and_8_out, instr[15], ~instr[14], ~instr[12]);  // AND_Gate
  and X_ABC_prime_D_prime (ALUcontrol[3], instr[15], instr[14], ~instr[13], ~instr[12]);  // AND_Gate
  or Z (ALUcontrol[1], instr[13], and_5_out, and_2_out, and_3_out);
  or W (ALUcontrol[0], and_6_out, and_7_out, and_8_out);
  and u_ADD (AND, ~instr[15], ~instr[14], ~instr[13], ~instr[12]);  // AND_Gate
  or Y (ALUcontrol[2], and_1_out, and_4_out);
  and u_ADDI (ADDI, ~instr[15], ~instr[14], instr[13], instr[12]);  // AND_Gate
  and ADD_2 (ADD, ~instr[15], ~instr[14], instr[13], ~instr[12]);  // AND_Gate
  and u_SUB (SUB, ~instr[15], instr[14], instr[13], ~instr[12]);  // AND_Gate
  and u_SLT (SLT, ~instr[15], instr[14], instr[13], instr[12]);  // AND_Gate
  and and_9 (and_9_out, ~instr[13], ~instr[12]);  // AND_Gate
  and and_10 (and_10_out, ~instr[14], ~instr[13]);  // AND_Gate
  and and_11 (and_11_out, ~instr[14], ~instr[12]);  // AND_Gate
  and and_12 (and_12_out, ~instr[15], ~instr[14]);  // AND_Gate
  and and_13 (and_13_out, ~instr[15], instr[13]);  // AND_Gate
  and and_14 (BEQ, instr[15], instr[14], instr[13], ~instr[12]);  // AND_Gate
  and u_BNE (BNE, instr[15], instr[14], ~instr[13], instr[12]);  // AND_Gate
  and and_15 (and_15_out, ~instr[15], ~instr[14], ~instr[13]);  // AND_Gate
  and and_16 (and_16_out, instr[15], ~instr[12]);  // AND_Gate
  and and_17 (and_17_out, instr[14], instr[13]);
  or or_1 (RegWrite, and_12_out, and_9_out, and_10_out, and_13_out);
  and A_prime_BC_prime (A_prime_BC_prime_out, ~instr[15], instr[14], ~instr[13]);  // AND_Gate
  and AB_prime_D (AB_prime_D_out, instr[15], ~instr[14], instr[12]);  // AND_Gate
  and B_prime_CD (B_prime_CD_out, ~instr[14], instr[13], instr[12]);  // AND_Gate
  or or_2 (RegDst, and_15_out, and_11_out, and_16_out, and_17_out);
  and u_J (J, instr[15], instr[14], instr[13], instr[12]);
  and and_18 (MemRead, ~instr[15], instr[14], ~instr[13], ~instr[12]);  // AND_Gate
  or or_3 (ALUSrc, A_prime_BC_prime_out, AB_prime_D_out, B_prime_CD_out);
  and and_19 (MemWrite, ~instr[15], instr[14], ~instr[13], instr[12]);  // AND_Gate

  assign immediate = instr[5:0];
  assign iumpAddress = instr[7:0];
  assign MemtoReg = MemRead;
  assign Rd = instr[5:3];
  assign Rs = instr[11:9];
  assign Rt = instr[8:6];

  // Other names for the same wires on the sheet: b0 = instr[0]; Instruction[15:0] = instr;
  //   JumpAddress[7:0] = instr[7:0]; b1 = instr[1]; b2 = instr[2]; b3 = instr[3]; b4 = instr[4]; b5 = instr[5];
  //   b12 = instr[12]; D = instr[12]; b13 = instr[13]; C = instr[13]; B = instr[14]; b14 = instr[14]; A = instr[15];
  //   b15 = instr[15]; b6 = instr[6]; b7 = instr[7]; LW = MemRead; b9 = instr[9]; b10 = instr[10]; b11 = instr[11];
  //   b8 = instr[8]; SW = MemWrite

  // Notes on the sheet:
  //   W= Σm(2,3,4,5,6,7,8,13,14) = A'B'C'D+BCD+AB'D'
  //   Y= Σm(6,7,9,12,13,14) =BC+AB+AC'D
  //   Z= Σm(2,3,4,5,6,7,8,13,14) = C+A'B+BD+AB'D'
  //   X= Σm(12) =ABC'D'
  //   RegWrite= Σm(0,1,2,3,4,6,7,8,9,12) =A'B'+C'D'+B'C'+A'C
  //   ALUSrc= A'BC'+AB'D+B'CD			
  //   RegDst=A'B'C'+B'D'+AD'+BC
endmodule

module Test_Cases__XXX_FILL_IN (
  input  [7:0] PC,
  input  [3:0] testCase,
  output [15:0] instr,
  output [7:0] ExpectedR1,
  output [7:0] ExpectedR2,
  output [7:0] ExpectedR3,
  output [7:0] ExpectedR4,
  output [7:0] ExpectedR5,
  output [7:0] ExpectedR6,
  output [7:0] ExpectedR7,
  output [7:0] MaxPC
);

  wire case0, case1, case2, case3, case4, case5, case6, case7, case8, case9, case10, case11, case12, case13,
       case14, case15;
  wire [7:0] \case ;

  Decoder #(.select(4), .enable("false")) decoder_1 (
    .out0(case0), .out1(case1), .out2(case2), .out3(case3), .out4(case4), .out5(case5), .out6(case6),
    .out7(case7), .out8(case8), .out9(case9), .out10(case10), .out11(case11), .out12(case12), .out13(case13),
    .out14(case14), .out15(case15), .sel(testCase));
  assign \case  = {{4{1'b0}}, testCase};  // Bit_Extender bit_extender_1
  ROM #(.dataWidth(16)) rom_1 (.addr(PC), .data(instr), .sel(case0));
  ROM #(.dataWidth(16)) rom_2 (.addr(PC), .data(instr), .sel(case1));
  ROM #(.dataWidth(16)) rom_3 (.addr(PC), .data(instr), .sel(case2));
  ROM #(.dataWidth(16)) rom_4 (.addr(PC), .data(instr), .sel(case3));
  ROM #(.dataWidth(16)) rom_5 (.addr(PC), .data(instr), .sel(case4));
  ROM #(.dataWidth(16)) rom_6 (.addr(PC), .data(instr), .sel(case5));
  ROM #(.dataWidth(16)) rom_7 (.addr(PC), .data(instr), .sel(case6));
  ROM #(.dataWidth(16)) rom_8 (.addr(PC), .data(instr), .sel(case7));
  ROM #(.dataWidth(16)) rom_9 (.addr(PC), .data(instr), .sel(case8));
  ROM #(.dataWidth(16)) rom_10 (.addr(PC), .data(instr), .sel(case9));
  ROM rom_11 (.addr(\case ), .data(ExpectedR1), .sel(1'b1));
  ROM rom_12 (.addr(\case ), .data(ExpectedR2), .sel(1'b1));
  ROM rom_13 (.addr(\case ), .data(ExpectedR3), .sel(1'b1));
  ROM rom_14 (.addr(\case ), .data(ExpectedR4), .sel(1'b1));
  ROM rom_15 (.addr(\case ), .data(ExpectedR5), .sel(1'b1));
  ROM rom_16 (.addr(\case ), .data(ExpectedR6), .sel(1'b1));
  ROM rom_17 (.addr(\case ), .data(ExpectedR7), .sel(1'b1));
  ROM rom_18 (.addr(\case ), .data(MaxPC), .sel(1'b1));

  // Other names for the same wires on the sheet: Instruction[15:0] = instr

  // Notes on the sheet:
  //   Upload Test Cases!!!
  //   slide.4.2.txt.asm
  //   gcd.txt.asm
  //   fib.txt.asm
  //   div.txt.asm
  //   summation.txt.asm
  //   pipeline.short.txt
  //   data.txt.asm
  //   sumByteMToN.txt
  //   mul.txt.asm
  //   sumByteArray.txt
  //   contents of rom_1 (hex, n*v repeats v):
  //   3041 3082 0 32c2 efff
  //   contents of rom_2 (hex, n*v repeats v):
  //   304e 3095 0 5040 5081 e28b 7298 0 0 d604 0 6288 f005 0 6450 f005 0 5082 4040 4081 40c2 313f 0 0 5103
  //   3140 3180 31c0 efff
  //   contents of rom_3 (hex, n*v repeats v):
  //   2008 3081 3100 0 0 5800 5881 2298 0 0 58c2 3901 0 0 396c 2088 20d0 da35 4041 4082 40c3 4104 4145
  //   4186 41c7 efff
  //   contents of rom_4 (hex, n*v repeats v):
  //   3247 3483 0 5040 5081 0 4040 4081 2018 2060 0 0 78a8 0 0 da04 0 68a0 36c1 f00a 50c2 5103 efff
  //   contents of rom_5 (hex, n*v repeats v):
  //   3041 3082 30c3 3104 3145 5040 5081 50c2 5103 5144 5005 3040 3080 0 0 44c0 0 0 e60d 0 7620 0 0 e802 0
  //   60d8 0 0 22c8 3481 f00d 0 5441 4040 4081 40c2 4103 4144 4185 41c6 efff
  //   contents of rom_6 (hex, n*v repeats v):
  //   3041 3082 0 5041 5082 efff
  //   contents of rom_7 (hex, n*v repeats v):
  //   3062 0 0 2248 0 0 2248 0 0 327e 0 0 5040 4040 4081 40c2 4103 4144 4185 41c6 efff
  //   contents of rom_8 (hex, n*v repeats v):
  //   3042 308a 2018 2020 2068 0 0 2758 6960 3b41 0 0 dab8 0 5041 5082 50c3 5104 5145 5186 51c7 efff
  //   contents of rom_9 (hex, n*v repeats v):
  //   3045 3088 0 5040 5081 2018 3181 3104 0 5a8 0 0 ea02 0 2658 2248 2db0 393f 0 0 d833 0 4040 4081 50c2
  //   efff
  //   contents of rom_10 (hex, n*v repeats v):
  //   3044 5040 3045 5041 3046 5042 3047 5043 3048 5044 3049 5045 3040 5046 3044 3085 30c6 3107 3148 3189
  //   31c0 5040 5081 50c2 5103 5144 5185 51c6 3140 3180 31c6 4b00 0 0 2d30 3b41 0 0 dbf8 5f80 4040 4081
  //   40c2 4103 4144 4185 41c6 efff
  //   contents of rom_11 (hex, n*v repeats v):
  //   1 e 1 7 1 1 86 2 5 4 0 7
  //   contents of rom_12 (hex, n*v repeats v):
  //   2 15 1 3 2 2 0 a 8 5 0 3
  //   contents of rom_13 (hex, n*v repeats v):
  //   3 7 2 2 3 0 0 2c 28 6 0 2
  //   contents of rom_14 (hex, n*v repeats v):
  //   0 ff 3 1 4 0 0 d4 0 7 0 1
  //   contents of rom_15 (hex, n*v repeats v):
  //   0 0 5 1 5 0 0 a 8 8 0 1
  //   contents of rom_16 (hex, n*v repeats v):
  //   0 0 8 5*0 10 9
  //   contents of rom_17 (hex, n*v repeats v):
  //   0 0 d 0 f 4*0 27
  //   contents of rom_18 (hex, n*v repeats v):
  //   6 1e 1b 18 2a 7 16 17 1b 32
  //   Expected Results!
  //   Submission by Lwin Moe, Linh Pham, and Rongjie Mai
endmodule
